# Fritzing sketch 555-conductivity (saved by Fritzing 1.0.1rc)
breadboards: 1

parts:
  U1 = 555 Timer [package="DIP8 [THT]"]
  C1 = Electrolytic Capacitor [capacitance=0.1µF voltage=35V package="0807 [SMD, electrolytic]"]
  R1 = Resistor [tolerance=±5% resistance=1k package="2512 [SMD]"]  # not connected
  C2 = Electrolytic Capacitor [capacitance=100μF voltage=35V package="0807 [SMD, electrolytic]"]
  Speaker = SPEAKER [package=pcb_mount_speaker]
  3V = Battery Holders [package=battcom_20mm_pth]

nets:
  N1: U1.Trigger, U1.Threshold, C1.+
  N2: U1.Output, C2.+
  N3: U1.Reset, U1.Vcc_Supply_Voltage, Speaker.+
  N4: C1.-, 3V.+, 3V.-
  N5: C2.-, Speaker.-

notes:
  C1: 0.1uF
  R1: 1K
  C2: 100 uF
  Probes
